# Fritzing sketch Blink (saved by Fritzing 0.8.5b)

parts:
  Parte1 = Arduino Uno (Rev3)
  LED1 = LED - 5mm [color="Red (633nm)" package="5 mm [THT]"]

nets:
  N1: Parte1.D13/SCK, LED1.anode
  N2: Parte1.GND, LED1.cathode
