# Fritzing sketch Button (saved by Fritzing 0.8.5b)
breadboards: 1

parts:
  Parte1 = Arduino Uno (Rev3)
  LED1 = LED - 5mm [color="Red (633nm)" package="5 mm [THT]"]
  S1 = Pushbutton [package="[THT]"]
  R1 = Resistor [tolerance=±5% resistance=10k package=THT]

nets:
  N1: Parte1.D13/SCK, LED1.anode
  N2: Parte1.GND, LED1.cathode, R1.Pin_1
  N3: Parte1.D2, S1.Pin_3, S1.Pin_4, R1.Pin_0
  N4: Parte1.5V, S1.Pin_1, S1.Pin_2
