# Fritzing sketch ldryspeaker (saved by Fritzing 0.9.3b)
breadboards: 1

parts:
  SP1 = SPEAKER [package=pcb_mount_speaker]
  R1 = Photocell (LDR) [package=THT]
  Componente1 = Arduino Uno (Rev3) - ICSP
  R2 = Resistor [tolerance=±5% resistance=10k package=THT]

nets:
  N1: SP1.+, Componente1.GND, R2.Pin_1
  N2: SP1.-, Componente1.A0
  N3: R1.pin_0, Componente1.5V
  N4: R1.pin_1, Componente1.A1, R2.Pin_0
