# Fritzing sketch 4Motores_DKElectronics (saved by Fritzing 0.9.3b)

parts:
  M1 = DC Motor
  M2 = DC Motor
  Componente2 = Adafruit Motor/Stepper/Servo Shield [part_number="Adafruit #1438"]
  M3 = DC Motor
  M4 = DC Motor

nets:
  N1: M1.pin_1, Componente2.M4A
  N2: M1.pin_2, Componente2.M4B
  N3: M2.pin_1, Componente2.M1A
  N4: M2.pin_2, Componente2.M1B
  N5: Componente2.M2A, M3.pin_2
  N6: Componente2.M3A, M4.pin_2
  N7: Componente2.M3B, M4.pin_1

custom parts:
  Adafruit Motor/Stepper/Servo Shield: The original Adafruit Motorshield kit is one of our most beloved kits, which is why we decided to make something even better. We have upgraded the shield kit to make the bestest, easiest way to drive DC and Stepper motors. This shield will make quick work of your next robotics project! We kept the ability to drive up to 4 DC motors or 2 stepper motors, but added many improvements: Instead of a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
