# Fritzing sketch rgbled (saved by Fritzing 0.9.3b)
breadboards: 1

parts:
  R1 = Resistor [tolerance=±5% resistance=220 package=THT]
  R2 = Resistor [tolerance=±5% resistance=220 package=THT]
  R3 = Resistor [tolerance=±5% resistance=220 package=THT]
  LED1 = RGB LED - (4 legs) [package="5 mm [THT]"]
  Componente1 = Arduino Uno (Rev3)  # not connected

nets:
  N1: R1.Pin_0, LED1.red_cathode
  N2: R2.Pin_0, LED1.green_cathode
  N3: R3.Pin_0, LED1.blue_cathode
